# Fritzing sketch circuit (saved by Fritzing 0.9.2b)
breadboards: 2

parts:
  부품1 = Arduino Uno (Rev3)
  LED1 = LED - 5mm [color="Red (633nm)" package="5 mm [THT]"]
  LED2 = LED - 5mm [color="Red (633nm)" package="5 mm [THT]"]
  LED3 = LED - 5mm [color="Red (633nm)" package="5 mm [THT]"]
  LED6 = LED - 5mm [color="Red (633nm)" package="5 mm [THT]"]
  LED7 = LED - 5mm [color="Red (633nm)" package="5 mm [THT]"]
  LED8 = LED - 5mm [color="Red (633nm)" package="5 mm [THT]"]
  LED9 = LED - 5mm [color="Red (633nm)" package="5 mm [THT]"]
  LED10 = LED - 5mm [color="Red (633nm)" package="5 mm [THT]"]
  LED11 = LED - 5mm [color="Red (633nm)" package="5 mm [THT]"]
  LED12 = LED - 5mm [color="Red (633nm)" package="5 mm [THT]"]
  LED13 = LED - 5mm [color="Red (633nm)" package="5 mm [THT]"]
  LED14 = LED - 5mm [color="Red (633nm)" package="5 mm [THT]"]
  R1 = Resistor [tolerance=±5% resistance=220 package=THT]
  R2 = Resistor [tolerance=±5% resistance=220 package=THT]
  R3 = Resistor [tolerance=±5% resistance=220 package=THT]
  R4 = Resistor [tolerance=±5% resistance=220 package=THT]
  R5 = Resistor [tolerance=±5% resistance=220 package=THT]
  R6 = Resistor [tolerance=±5% resistance=220 package=THT]
  R7 = Resistor [tolerance=±5% resistance=220 package=THT]
  R8 = Resistor [tolerance=±5% resistance=220 package=THT]
  R9 = Resistor [tolerance=±5% resistance=220 package=THT]
  R10 = Resistor [tolerance=±5% resistance=220 package=THT]
  R11 = Resistor [tolerance=±5% resistance=220 package=THT]
  R12 = Resistor [tolerance=±5% resistance=220 package=THT]  # not connected
  R13 = Rotary Potentiometer (Small) [maximum_resistance=100kΩ package=THT]
  S1 = Pushbutton [package=THT]
  S2 = Pushbutton [package=THT]
  R14 = Resistor [tolerance=±5% resistance=220 package="0603 [SMD]"]
  R15 = Resistor [tolerance=±5% resistance=220 package="0603 [SMD]"]

nets:
  N1: 부품1.A0, R13.wiper
  N2: 부품1.A1, S1.leg0, R15.Pin_1
  N3: 부품1.A2, S2.leg0, R14.Pin_1
  N4: 부품1.D8, R6.Pin_1
  N5: 부품1.D9_PWM, R5.Pin_1
  N6: 부품1.D10_PWM/SS, R4.Pin_1
  N7: 부품1.D11_PWM/MOSI, R3.Pin_1
  N8: 부품1.D12/MISO, R1.Pin_1
  N9: 부품1.D13/SCK, R2.Pin_0
  N10: 부품1.D2, R11.Pin_1
  N11: 부품1.D4, R10.Pin_1
  N12: 부품1.D5_PWM, R9.Pin_1
  N13: 부품1.D6_PWM, R8.Pin_0
  N14: 부품1.D7, R7.Pin_1
  N15: 부품1.5V, R13.leg2, R14.Pin_0, R15.Pin_0
  N16: 부품1.GND, LED1.cathode, LED2.cathode, LED3.cathode, LED6.cathode, LED7.cathode, LED8.cathode, LED9.cathode, LED10.cathode, LED11.cathode, LED12.cathode, LED13.cathode, LED14.cathode, R13.leg1, S1.leg1, S2.leg1
  N17: LED1.anode, R4.Pin_0
  N18: LED2.anode, R3.Pin_0
  N19: LED3.anode, R7.Pin_0
  N20: LED6.anode, R5.Pin_0
  N21: LED7.anode, R6.Pin_0
  N22: LED8.anode, LED10.anode, R1.Pin_0, R8.Pin_1
  N23: LED9.anode, R2.Pin_1
  N24: LED11.anode, R9.Pin_0
  N25: LED12.anode, R10.Pin_0
  N26: LED13.anode, R11.Pin_0
